# Fritzing sketch breadboard (saved by Fritzing 0.9.4)
breadboards: 1

parts:
  M1 = Stepper Motor - Bipolar
  C1 = Electrolytic Capacitor [capacitance=0.1mF voltage=20V package="100 mil [THT, electrolytic]"]
  U1 = mystery part, 7 pins [chip_label=?]
  U2 = mystery part, 8 pins [chip_label=?]
  U3 = mystery part, 8 pins [chip_label=?]
  U4 = mystery part, 7 pins [chip_label=?]  # not connected
  Power_plug1 = Power plug

nets:
  N1: M1.A, U3.pin6
  N2: M1.C, U3.pin5
  N3: M1.B, U3.pin4
  N4: M1.D, U3.pin3
  N5: C1.-, U3.pin7, Power_plug1.GND
  N6: C1.+, U3.pin8, Power_plug1.VCC
  N7: U1.pin2, U2.pin7
  N8: U1.pin3, U2.pin8
  N9: U1.pin5, U2.pin5, U2.pin6
  N10: U1.pin6, U3.pin1
