# Fritzing sketch permaproto (saved by Fritzing 0.9.4)

parts:
  M1 = Stepper Motor - Bipolar
  C1 = Electrolytic Capacitor [capacitance=0.1mF voltage=20V package="100 mil [THT, electrolytic]"]  # not connected
  J2 = screw terminal, 4 pins
  proto2 = Adafruit_PermaProto_1_4_Board
  S2 = Pushbutton [package="[THT]"]
  Power_plug2 = Power plug
  U5 = mystery part, 7 pins [chip_label=?]  # not connected
  U6 = mystery part, 7 pins [chip_label=?]  # not connected
  U7 = mystery part, 8 pins [chip_label=?]  # not connected
  U8 = mystery part, 8 pins [chip_label=?]  # not connected

nets:
  N1: M1.A, J2.pin4
  N2: M1.C, J2.pin3
  N3: M1.B, J2.pin2
  N4: M1.D, J2.pin1
  N5: proto2.connectorA8, proto2.connectorX8
  N6: proto2.connectorA14, Power_plug2.GND
  N7: proto2.connectorA15, Power_plug2.VCC
  N8: proto2.connectorF4, proto2.connectorF8
  N9: proto2.connectorG5, proto2.connectorG9
  N10: proto2.connectorI10, proto2.connectorI11
  N11: proto2.connectorJ1, proto2.connectorX1
  N12: proto2.connectorJ2, proto2.connectorJ10
  N13: S2.Pin_1, S2.Pin_2
  N14: S2.Pin_3, S2.Pin_4

notes:
  Main ground wire goes underneath the board. Wire it in last. All other wires are on top. Button pin must be configured pull-up.
